# Fritzing sketch sketch1 (saved by Fritzing 0.9.3b)
perfboards: 1

parts:
  Part1 = Arduino Nano (Rev3.0)
  VCC1 = Battery  # not connected
  BT1 = Bluetooth HC-06u [package=THT]
  Part2 = Standard LCD 16x2 white on blue [part_number=181]
  R1 = Rotary Potentiometer (Small) [maximum_resistance=100kΩ package=THT]
  R2 = Resistor [tolerance=±5% resistance=220 package=THT]
  S1 = Toggle Switch [package=THT]
  S2 = Pushbutton [package="[THT]"]
  Part3 = SRF05 Ultrasonic Rangefinder
  R3 = Resistor [tolerance=±5% resistance=220 package=THT]
  R4 = Resistor [tolerance=±5% resistance=220 package=THT]

nets:
  N1: Part1.D1/TX, BT1.RXD
  N2: Part1.D0/RX, BT1.TXD
  N3: Part1.D2, Part2.RS
  N4: Part1.D3, Part2.E
  N5: Part1.D4, Part2.DB4
  N6: Part1.D5, Part2.DB5
  N7: Part1.D6, Part2.DB6
  N8: Part1.D7, Part2.DB7
  N9: Part1.D8, S2.Pin_1, S2.Pin_2
  N10: Part1.D9, Part3.Trig
  N11: Part1.D10, Part3.Echo
  N12: Part1.VIN, S1.COM
  VCC: BT1.VCC, Part2.VDD
  GND: BT1.GND, Part2.VSS
  N13: Part2.V0, R1.wiper
  N14: Part2.LED+, R2.Pin_1, R3.Pin_1
  N15: R2.Pin_0, R3.Pin_0
  N16: S2.Pin_4, R4.Pin_0

custom parts:
  Bluetooth HC-06u: Bluetooth HC-06 - face up, pins down 16.5mm x 37.5mm PCB
  Standard LCD 16x2 white on blue: Standard HD44780 LCDs are useful for creating standalone projects. * 16 characters wide, 2 rows * White text on blue background * Connection port is 0.1" pitch, single row for easy breadboarding and wiring
